# Fritzing sketch varal (saved by Fritzing 0.9.6b)
breadboards: 1

parts:
  M1 = gear-motor
  M2 = gear-motor
  U1 = POT [package=alps_pot]
  R1 = Photocell (LDR) [package=THT]
  YL-83_-_Detection_Board1 = YL-83 Rain Sensor - Detection Board
  YL-83_-_Control_Board2 = YL-83 Rain Sensor - Control Board
  Part1 = Arduino Uno (Rev3)
  U2 = L9110 H-bridge module [part_number="L9110 H-bridge"]
  R2 = Resistor [tolerance=±5% power=0.25 resistance=10k package=THT]
  VCC1 = Battery block 9V
  JL012-13-5_1 = JL012-13-5.2 Lever (Limit) Switch SPDT + NO + NC [part_number=JL012-13-5.2]
  JL012-13-5_2 = JL012-13-5.2 Lever (Limit) Switch SPDT + NO + NC [part_number=JL012-13-5.2]
  Part3 = FC-03

nets:
  N1: M1.pin_1, U2.MOTOR_B-B
  N2: M1.pin_2, U2.MOTOR_B-A
  N3: M2.pin_1, U2.MOTOR_A-B
  N4: M2.pin_2, U2.MOTOR_A-A
  VCC: U1.E, R1.pin_1, YL-83_-_Control_Board2.VCC, Part1.5V, JL012-13-5_1.C, JL012-13-5_2.C, Part3.VCC
  N5: U1.S, Part1.A5/SCL
  GND: U1.A, YL-83_-_Control_Board2.GND, Part1.A1, Part1.GND, U2.GND, R2.Pin_1, VCC1.-, Part3.GND
  N6: R1.pin_0, R2.Pin_0
  N7: YL-83_-_Detection_Board1.POS, YL-83_-_Control_Board2.POS
  N8: YL-83_-_Detection_Board1.NEG, YL-83_-_Control_Board2.NEG
  N9: YL-83_-_Control_Board2.AO, Part1.A0
  N10: Part1.D8, U2.A-IA
  N11: Part1.D10_PWM/SS, U2.A-IB
  N12: Part1.D11_PWM/MOSI, U2.B-IB
  N13: Part1.D12/MISO, U2.B-IA
  N14: Part1.D3_PWM, JL012-13-5_2.NO
  N15: Part1.D4, Part3.D0
  N16: U2.VCC, VCC1.+

custom parts:
  YL-83 Rain Sensor - Detection Board: The YL-83 is a rain sensor that has more resistance when dry and less resistance when wet. The module runs at 5V.
  YL-83 Rain Sensor - Control Board: The YL-83 is a rain sensor that has more resistance when dry and less resistance when wet. The module runs at 5V.
  JL012-13-5.2 Lever (Limit) Switch SPDT + NO + NC: Micro Switch; Model No.: JL012-13.5-2; Actuator Action: Momentary; Actuator Type: Hinge Lever; Contact Configuration: 1NO, 1NC (SPDT) Temperature -25~65℃；Relative humidity: below 85%; Rate Voltage: 125V AC; Rated Current: 1A.
  FC-03: FC-03, LM393 IR Speed Sensor Encoder By Nandan
